// Logisim project hw2_get.circ as structural Verilog
module RS (
  input  R,
  input  C,
  input  S,
  output Q,
  output notQ
);

  wire and_1_out, and_2_out;

  and and_1 (and_1_out, R, C);
  and and_2 (and_2_out, C, S);
  nor nor_1 (Q, and_1_out, notQ);
  nor nor_2 (notQ, Q, and_2_out);
endmodule

module JK (
  input  J,
  input  C,
  input  K,
  input  reset,
  output Q,
  output notQ
);

  wire and_1_out, and_2_out, and_3_out, not_1_out, not_2_out, or_1_out, or_2_out, rs_1_notq, rs_1_q;

  and and_1 (and_1_out, notQ, J);
  and and_2 (and_2_out, K, Q);
  or or_1 (or_1_out, C, reset);
  and and_3 (and_3_out, and_1_out, not_1_out);
  not not_1 (not_1_out, reset);
  or or_2 (or_2_out, reset, and_2_out);
  RS rs_1 (.R(and_3_out), .C(or_1_out), .S(or_2_out), .Q(rs_1_q), .notQ(rs_1_notq));
  not not_2 (not_2_out, or_1_out);
  RS rs_2 (.R(rs_1_q), .C(not_2_out), .S(rs_1_notq), .Q(Q), .notQ(notQ));
endmodule

// JRprotiv
module JKprotiv (
  input  J,
  input  C,
  input  K,
  input  reset,
  output Q,
  output notQ
);

  wire and_1_out, and_2_out, and_3_out, not_1_out, not_2_out, or_1_out, or_2_out, rs_1_notq, rs_1_q;

  and and_1 (and_1_out, notQ, J);
  and and_2 (and_2_out, K, Q);
  or or_1 (or_1_out, C, reset);
  or or_2 (or_2_out, and_1_out, reset);
  not not_1 (not_1_out, reset);
  and and_3 (and_3_out, not_1_out, and_2_out);
  RS rs_1 (.R(or_2_out), .C(or_1_out), .S(and_3_out), .Q(rs_1_q), .notQ(rs_1_notq));
  not not_2 (not_2_out, or_1_out);
  RS rs_2 (.R(rs_1_q), .C(not_2_out), .S(rs_1_notq), .Q(Q), .notQ(notQ));
endmodule

module counter (
);

  wire and_1_out, and_2_out, and_3_out, and_4_out, jk_1_notq, jk_1_q, jk_2_notq, jk_2_q, jkprotiv_1_notq,
       jkprotiv_1_q, jkprotiv_2_notq, jkprotiv_2_q, not_1_out, or_1_out, or_2_out, RESET_out, x1_1_out;

  Button RESET (.out(RESET_out));
  Clock x1_1 (.out(x1_1_out));
  not not_1 (not_1_out, x1_1_out);
  or or_1 (or_1_out, x1_1_out, not_1_out);
  or or_2 (or_2_out, RESET_out, and_4_out);
  JKprotiv jkprotiv_1 (
    .J(or_1_out), .C(x1_1_out), .K(or_1_out), .reset(or_2_out), .Q(jkprotiv_1_q), .notQ(jkprotiv_1_notq));
  LED Q0 (.in(jkprotiv_1_notq));
  and and_1 (and_1_out, not_1_out, jkprotiv_1_q);
  LED Q1 (.in(jk_1_notq));
  JK jk_1 (.J(and_1_out), .C(x1_1_out), .K(and_1_out), .reset(or_2_out), .Q(jk_1_q), .notQ(jk_1_notq));
  and and_2 (and_2_out, and_1_out, jk_1_q);
  JKprotiv jkprotiv_2 (
    .J(and_2_out), .C(x1_1_out), .K(and_2_out), .reset(or_2_out), .Q(jkprotiv_2_q), .notQ(jkprotiv_2_notq));
  LED Q2 (.in(jkprotiv_2_notq));
  and and_3 (and_3_out, and_2_out, jkprotiv_2_q);
  JK jk_2 (.J(and_3_out), .C(x1_1_out), .K(and_3_out), .reset(or_2_out), .Q(jk_2_q), .notQ(jk_2_notq));
  LED Q3 (.in(jk_2_notq));
  and and_4 (and_4_out, x1_1_out, jk_2_q, jkprotiv_2_q, jk_1_q, jkprotiv_1_q);
endmodule

module sqrt (
  input  in7,
  input  in6,
  input  in5,
  input  in4,
  input  in3,
  input  in2,
  input  in1,
  input  in0,
  output out3,
  output ou2,
  output out1,
  output out0
);

  wire and_1_out, and_2_out, and_3_out, and_4_out, and_5_out, and_6_out, and_7_out, and_8_out, and_9_out,
       and_10_out, and_11_out, and_12_out, and_13_out, and_14_out, and_15_out, and_16_out, and_17_out,
       and_18_out, and_19_out, and_20_out, and_21_out, and_22_out, and_23_out, and_24_out, and_25_out,
       and_26_out, and_27_out, and_28_out, and_29_out, and_30_out, and_31_out, and_32_out, and_33_out,
       and_34_out, and_35_out, and_36_out, and_37_out, and_38_out, and_39_out, and_40_out, not_1_out,
       not_2_out, not_3_out, not_4_out, not_5_out, not_6_out;

  not not_1 (not_1_out, in7);
  not not_2 (not_2_out, in6);
  not not_3 (not_3_out, in5);
  not not_4 (not_4_out, in4);
  not not_5 (not_5_out, in3);
  not not_6 (not_6_out, in2);
  or or_1 (out3, in6, in7);
  and and_1 (and_1_out, not_2_out, in4);
  and and_2 (and_2_out, not_2_out, in5);
  and and_3 (and_3_out, in7, in6);
  and and_4 (and_4_out, not_1_out, not_2_out, not_4_out, in2);
  and and_5 (and_5_out, not_2_out, not_3_out, not_4_out, in3);
  and and_6 (and_6_out, not_1_out, in5, in2);
  and and_7 (and_7_out, not_1_out, in5, in3);
  and and_8 (and_8_out, not_1_out, in5, in4);
  and and_9 (and_9_out, in7, not_2_out, not_3_out, not_4_out);
  and and_10 (and_10_out, in7, in6, in2);
  and and_11 (and_11_out, in7, in6, in3);
  and and_12 (and_12_out, in7, in6, in4);
  and and_13 (and_13_out, in7, in6, in5);
  and and_14 (and_14_out, not_2_out, not_3_out, not_4_out, not_6_out, in0);
  and and_15 (and_15_out, not_2_out, not_3_out, not_4_out, not_6_out, in1);
  and and_16 (and_16_out, not_1_out, not_2_out, not_3_out, in3, in0);
  and and_17 (and_17_out, not_1_out, not_2_out, not_3_out, in3, in1);
  and and_18 (and_18_out, not_2_out, not_3_out, not_4_out, in3, in2);
  and and_19 (and_19_out, not_1_out, in4, in3, in0);
  and and_20 (and_20_out, not_1_out, in4, in3, in1);
  and and_21 (and_21_out, not_1_out, in4, in3, in2);
  and and_22 (and_22_out, not_1_out, in5, not_4_out, not_5_out, not_6_out);
  and and_23 (and_23_out, not_2_out, in5, in4, in0);
  and and_24 (and_24_out, not_2_out, in5, in4, in1);
  and and_25 (and_25_out, not_2_out, in5, in4, in2);
  and and_26 (and_26_out, not_2_out, in5, in4, in3);
  and and_27 (and_27_out, not_1_out, in6, not_3_out, in4, in0);
  and and_28 (and_28_out, not_1_out, in6, not_3_out, in4, in1);
  and and_29 (and_29_out, not_1_out, in6, not_3_out, in4, in2);
  and and_30 (and_30_out, not_1_out, in6, not_3_out, in4, in3);
  and and_31 (and_31_out, in7, not_2_out, not_3_out, not_4_out);
  and and_32 (and_32_out, in7, not_3_out, not_4_out, not_5_out, not_6_out);
  and and_33 (and_33_out, in7, in5, in3, in0);
  and and_34 (and_34_out, in7, in5, in3, in1);
  and and_35 (and_35_out, in7, in5, in3, in2);
  and and_36 (and_36_out, in7, in5, in4);
  and and_37 (and_37_out, in7, in6, in5, in0);
  and and_38 (and_38_out, in7, in6, in5, in1);
  and and_39 (and_39_out, in7, in6, in5, in2);
  and and_40 (and_40_out, in7, in6, in5, in3);
  or or_2 (ou2, and_1_out, and_2_out, and_3_out);
  or or_3 (out1, and_4_out, and_5_out, and_6_out, and_7_out, and_8_out, and_9_out, and_10_out, and_11_out, and_12_out, and_13_out);
  or or_4 (out0, and_14_out, and_15_out, and_16_out, and_17_out, and_18_out, and_19_out, and_20_out, and_21_out, and_22_out, and_23_out, and_24_out, and_25_out, and_26_out, and_27_out, and_28_out, and_29_out, and_30_out, and_31_out, and_32_out, and_33_out, and_34_out, and_35_out, and_36_out, and_37_out, and_38_out, and_39_out, and_40_out);
endmodule
